# Fritzing sketch effect-midi.rp2040 (saved by Fritzing 0.9.5d)
breadboards: 1

parts:
  Mod1 = Raspberry Pi Pico
  R1 = Resistor [tolerance=±5% resistance=330 package="0603 [SMD]"]
  元件1 = ws2812b [package="smd 2812b"]

nets:
  N1: Mod1.pin_3, Mod1.pin_8, Mod1.pin_13, Mod1.pin_18, Mod1.pin_23, Mod1.pin_28, Mod1.pin_33, Mod1.pin_38, 元件1.VSS
  N2: Mod1.pin_10, R1.Pin_0
  N3: Mod1.pin_40, 元件1.VDD
  N4: R1.Pin_1, 元件1.DIN

notes:
  WS2812B
  330Ω

custom parts:
  Raspberry Pi Pico: Raspberry Pi Pico. Based around the RP2040 microcontroller the Pico is a low cost microcontroller device bringing Raspberry Pi quality, cost, and easy of use to the microcontroller space. Jan 2021, Split part in to two versions: tht (this one) and SMD. This one will drill holes for a .1 in header in pcb to allow plugging in the module as well as providing pads to solder the module to the top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
